# Fritzing sketch Esquema de conexiones (saved by Fritzing 0.9.0b)
breadboards: 1

parts:
  ARD_1 = Arduino Uno (Rev3)
  U2 = mystery part, 5 pins [chip_label="Mando Derecha"]
  U5 = mystery part, 5 pins [chip_label="Mando Izquierda"]
  J1 = Basic Servo
  J2 = Basic Servo
  J3 = Basic Servo
  J4 = Basic Servo

nets:
  N1: ARD_1.A0, U5.pin3
  N2: ARD_1.A2, U2.pin3
  N3: ARD_1.A3, U2.pin2
  N4: ARD_1.D9_PWM, J3.pulse
  N5: ARD_1.D10_PWM/SS, J4.pulse
  N6: ARD_1.D11_PWM/MOSI, J2.pulse
  GND: ARD_1.GND, U2.pin1, U5.pin1, J1.gnd, J2.gnd, J3.gnd, J4.gnd
  N7: ARD_1.D2, U5.pin4
  N8: ARD_1.D3_PWM, U2.pin4
  N9: ARD_1.D7, J1.pulse
  VCC: ARD_1.5V, U2.pin5, U5.pin5, J1.vcc, J3.vcc
  7.5V: ARD_1.VIN
  VCC_2: J2.vcc, J4.vcc
